# Fritzing sketch Autopaper (saved by Fritzing 0.9.2b)

parts:
  Часть2 = SRF05 Ultrasonic Rangefinder
  JP1 = Header 3 [package=screwterminal-3.5mm-3_lock.007s]
  U2 = G3VM-61E1 [package=g3vm-61e1]
  VCC1 = Battery block 9V  # not connected
  M1 = DC Motor
  Часть3 = Arduino Pro Mini v13

nets:
  N1: Часть2.VCC, JP1.3
  N2: Часть2.Trig, Часть3.D8
  N3: Часть2.Echo, Часть3.D7
  GND: Часть2.GND, U2.P$2, Часть3.GND
  N4: JP1.1, U2.P$1
  N5: JP1.2, Часть3.VCC
  N6: U2.P$3, Часть3.D4
  N7: U2.P$5, M1.pin_1
