# Fritzing sketch AutopaperNew (saved by Fritzing 0.9.2b)
breadboards: 1

parts:
  Часть4 = Arduino Pro Mini v13
  U3 = G3VM-61E1 [package=g3vm-61e1]
  Часть5 = SRF05 Ultrasonic Rangefinder
  M2 = DC Motor
  VCC2 = Battery block 9V

nets:
  GND: Часть4.GND, U3.P$2, Часть5.GND, VCC2.-
  VCC: Часть4.VCC, U3.P$1, U3.P$4, Часть5.VCC, M2.pin_2, VCC2.+
  N1: Часть4.D8, Часть5.Trig
  N2: Часть4.D7, Часть5.Echo
  N3: Часть4.D4, U3.P$3
  N4: U3.P$5, M2.pin_1
